// Logisim project inf1400Oblig1-3input-7dontcare.circ as structural Verilog: 1 circuit, main circuit main
module main (
  input  T,
  input  U,
  input  V
);

  wire not_1_out, T_prime_U_prime_V_prime_out, T_prime_V_prime_out, T_U_prime_V_prime_out, TU_out,
       TU_T_prime_V_prime_out, U_T_out, U_V_out, U_VT_prime_V_prime_T_out, V_prime_U_prime_out,
       V_U_prime_T_out, VT_prime_TV_prime_out;

  xnor VT_prime_TV_prime (VT_prime_TV_prime_out, T, V);
  or U_V (U_V_out, U, V);
  not not_1 (not_1_out, U);
  nand T_prime_U_prime_V_prime (T_prime_U_prime_V_prime_out, T, U_V_out);
  or U_VT_prime_V_prime_T (U_VT_prime_V_prime_T_out, U, VT_prime_TV_prime_out);
  or V_U_prime_T (V_U_prime_T_out, T, V, not_1_out);
  or U_T (U_T_out, T, U);
  and TU (TU_out, T, U);
  nor T_prime_V_prime (T_prime_V_prime_out, T, V);
  nor V_prime_U_prime (V_prime_U_prime_out, U, V);
  or TU_T_prime_V_prime (TU_T_prime_V_prime_out, TU_out, T_prime_V_prime_out);
  or T_U_prime_V_prime (T_U_prime_V_prime_out, T, V_prime_U_prime_out);
  _7_Segment_Display u_7_segment_display_1 (
    .g(U_T_out), .f(T_U_prime_V_prime_out), .a(U_VT_prime_V_prime_T_out), .b(T_prime_U_prime_V_prime_out),
    .e(TU_T_prime_V_prime_out), .d(U_VT_prime_V_prime_T_out), .c(V_U_prime_T_out));  // open: dp

  // Notes on the sheet:
  //   Istedenfor å bruke inputnavnene X0, X1, X2 har jeg heller brukt T, U, V
  //   Sannhetsverditabellen, k-maps og de logiske utrykkene er lagt til som pdf-filer
  //   Jeg syntes at 6 tallet som skulle vises av displayet var stydt så jeg valgte derfor å endre den slik at a også lyser, dette gjelder også for de andre kretsene
  //   g f a b
  //   e d c
  //   12 porter
endmodule
