// Logisim project inf1400Oblig1-4input.circ as structural Verilog: 1 circuit, main circuit main
module main (
  input  S,
  input  T,
  input  U,
  input  V
);

  wire not_1_out, not_2_out, or_1_out, or_2_out, or_3_out, or_4_out, S_prime_T_nTS_out, S_prime_T_prime_out,
       S_prime_T_prime_U_out, S_prime_U_prime_2_out, S_prime_U_prime_out, S_prime_U_SU_prime_out,
       S_prime_V_prime_SV_out, S_prime_V_U_prime_V_out, S_T_prime_V_TV_prime_out, S_U_V_out, ST_prime_SU_out,
       SU_prime_out, T_prime_S_prime_U_prime_V_prime_out, T_prime_S_prime_V_prime_T_prime_SV_out,
       T_prime_U_out, T_prime_V_prime_2_out, T_prime_V_prime_out, T_prime_V_prime_V_prime_U_TS_US_out,
       T_prime_V_TV_prime_out, T_U_out, TS_prime_U_prime_out, TS_US_out, TU_prime_TV_prime_out,
       TUV_prime_TU_prime_V_out, TVS_prime_U_TVSU_prime_out,
       TVS_prime_U_TVSU_prime_T_prime_S_prime_U_prime_V_prime_out, U_prime_V_prime_2_out,
       U_prime_V_prime_out, UT_prime_UV_prime_out, UV_prime_out, UV_prime_U_prime_V_out;

  not not_1 (not_1_out, T);
  not not_2 (not_2_out, U);
  or S_U_V (S_U_V_out, U, S, V);
  nand T_prime_V_prime (T_prime_V_prime_out, V, T);
  nor S_prime_U_prime (S_prime_U_prime_out, U, S);
  xor UV_prime_U_prime_V (UV_prime_U_prime_V_out, V, U);
  nand U_prime_V_prime (U_prime_V_prime_out, U, V);
  nand T_prime_U (T_prime_U_out, not_2_out, T);
  and UT_prime_UV_prime (UT_prime_UV_prime_out, U, T_prime_V_prime_out);
  or T_U (T_U_out, T, U);
  and TUV_prime_TU_prime_V (TUV_prime_TU_prime_V_out, T, UV_prime_U_prime_V_out);
  xor S_prime_T_nTS (S_prime_T_nTS_out, T, S);
  nand S_prime_U_prime_2 (S_prime_U_prime_2_out, S, U);
  xor S_prime_U_SU_prime (S_prime_U_SU_prime_out, U, S);
  xnor T_prime_V_TV_prime (T_prime_V_TV_prime_out, T, V);
  and TU_prime_TV_prime (TU_prime_TV_prime_out, U_prime_V_prime_out, T);
  nor U_prime_V_prime_2 (U_prime_V_prime_2_out, V, U);
  and TS_prime_U_prime (TS_prime_U_prime_out, T, S_prime_U_prime_out);
  xnor S_prime_V_prime_SV (S_prime_V_prime_SV_out, S, V);
  nand T_prime_S_prime_U_prime_V_prime (T_prime_S_prime_U_prime_V_prime_out, T, S_U_V_out);
  and ST_prime_SU (ST_prime_SU_out, S, T_prime_U_out);
  and T_prime_S_prime_V_prime_T_prime_SV (T_prime_S_prime_V_prime_T_prime_SV_out, not_1_out, S_prime_V_prime_SV_out);
  and TVS_prime_U_TVSU_prime (TVS_prime_U_TVSU_prime_out, S_prime_U_SU_prime_out, T, V);
  nor UV_prime (UV_prime_out, V, not_2_out);
  and S_prime_V_U_prime_V (S_prime_V_U_prime_V_out, V, S_prime_U_prime_2_out);
  or S_T_prime_V_TV_prime (S_T_prime_V_TV_prime_out, T_prime_V_TV_prime_out, U, S);
  nor T_prime_V_prime_2 (T_prime_V_prime_2_out, V, T);
  and TS_US (TS_US_out, S, T_U_out);
  and SU_prime (SU_prime_out, S, not_2_out);
  or TVS_prime_U_TVSU_prime_T_prime_S_prime_U_prime_V_prime (TVS_prime_U_TVSU_prime_T_prime_S_prime_U_prime_V_prime_out, T_prime_S_prime_U_prime_V_prime_out, TVS_prime_U_TVSU_prime_out);
  or T_prime_V_prime_V_prime_U_TS_US (T_prime_V_prime_V_prime_U_TS_US_out, T_prime_V_prime_2_out, UV_prime_out, TS_US_out);
  nor S_prime_T_prime (S_prime_T_prime_out, S, T);
  _7_Segment_Display u_7_segment_display_1 (
    .g(or_1_out), .f(or_4_out), .a(S_T_prime_V_TV_prime_out),
    .b(TVS_prime_U_TVSU_prime_T_prime_S_prime_U_prime_V_prime_out), .e(T_prime_V_prime_V_prime_U_TS_US_out),
    .d(or_2_out), .c(or_3_out));  // open: dp
  or or_1 (or_1_out, ST_prime_SU_out, UT_prime_UV_prime_out, TS_prime_U_prime_out);
  and S_prime_T_prime_U (S_prime_T_prime_U_out, U, S_prime_T_prime_out);
  or or_2 (or_2_out, S_prime_T_prime_U_out, SU_prime_out, T_prime_S_prime_V_prime_T_prime_SV_out, TUV_prime_TU_prime_V_out);
  or or_3 (or_3_out, S_prime_U_prime_out, S_prime_T_nTS_out, S_prime_V_U_prime_V_out);
  or or_4 (or_4_out, TU_prime_TV_prime_out, S, U_prime_V_prime_2_out);

  // Notes on the sheet:
  //   Valgt inputnavenen S, T, U, V fremfor X0, X1, X2, X3
  //   Sannhetsverditabellen, k-maps og de logiske utrykkene er lagt ved som pdf-er
  //   e, d, c
  //   g, f, a, b
  //   37 gates
endmodule
