// Logisim project inf1400Oblig1-3input.circ as structural Verilog: 1 circuit, main circuit main
module main (
  input  T,
  input  U,
  input  V
);

  wire not_1_out, not_2_out, or_1_out, T_prime_U_TU_prime_out, T_prime_UV_U_prime_V_prime_out,
       T_prime_V_prime_out, T_prime_V_prime_TV_out, T_U_prime_V_out, TU_prime_TV_prime_out,
       U_prime_V_prime_2_out, U_prime_V_prime_out, U_prime_V_prime_TU_prime_TV_prime_out,
       U_T_prime_V_TV_prime_out, UV_U_prime_V_prime_out, V_prime_U_out, V_prime_U_T_prime_U_TU_prime_out,
       V_prime_U_T_prime_V_prime_out, xnor_1_out;

  not not_1 (not_1_out, T);
  not not_2 (not_2_out, V);
  nand U_prime_V_prime (U_prime_V_prime_out, U, V);
  nor U_prime_V_prime_2 (U_prime_V_prime_2_out, V, U);
  and V_prime_U (V_prime_U_out, U, not_2_out);
  and TU_prime_TV_prime (TU_prime_TV_prime_out, U_prime_V_prime_out, T);
  xor T_prime_U_TU_prime (T_prime_U_TU_prime_out, T, U);
  nor T_prime_V_prime (T_prime_V_prime_out, T, V);
  xnor T_prime_V_prime_TV (T_prime_V_prime_TV_out, T, V);
  or U_T_prime_V_TV_prime (U_T_prime_V_TV_prime_out, T_prime_V_prime_TV_out, U);
  or V_prime_U_T_prime_U_TU_prime (V_prime_U_T_prime_U_TU_prime_out, V_prime_U_out, T_prime_U_TU_prime_out);
  or V_prime_U_T_prime_V_prime (V_prime_U_T_prime_V_prime_out, V_prime_U_out, T_prime_V_prime_out);
  xnor UV_U_prime_V_prime (UV_U_prime_V_prime_out, U, V);
  or U_prime_V_prime_TU_prime_TV_prime (U_prime_V_prime_TU_prime_TV_prime_out, TU_prime_TV_prime_out, U_prime_V_prime_2_out);
  xnor xnor_1 (xnor_1_out, T_prime_U_TU_prime_out, V);
  nand T_U_prime_V (T_U_prime_V_out, not_2_out, not_1_out, U);
  or T_prime_UV_U_prime_V_prime (T_prime_UV_U_prime_V_prime_out, not_1_out, UV_U_prime_V_prime_out);
  _7_Segment_Display u_7_segment_display_1 (
    .g(V_prime_U_T_prime_U_TU_prime_out), .f(U_prime_V_prime_TU_prime_TV_prime_out),
    .a(U_T_prime_V_TV_prime_out), .b(T_prime_UV_U_prime_V_prime_out), .e(V_prime_U_T_prime_V_prime_out),
    .d(or_1_out), .c(T_U_prime_V_out));  // open: dp
  or or_1 (or_1_out, V_prime_U_out, xnor_1_out);

  // Notes on the sheet:
  //   Sannhetsverditabellen, k-maps og de logiske utrykkene er lagt ved som pdf-filer
  //   e, d, c
  //   g, f, a, b
  //   18 gates
endmodule
