// Logisim project inf1400Oblig1-kladd.circ as structural Verilog: 1 circuit, main circuit main
module main (
  input  S,
  input  T,
  input  U,
  input  V
);

  wire and_1_out, and_2_out, and_3_out, and_4_out, and_5_out, and_6_out, and_7_out, and_8_out, and_9_out,
       and_10_out, and_11_out, and_12_out, nor_1_out, nor_2_out, not_1_out, not_2_out, not_3_out, not_4_out,
       or_1_out, or_2_out, or_3_out, or_4_out, or_5_out, or_6_out, or_7_out, s_prime_t_st_prime_out,
       s_u__prime_out, s_v__prime_out, S_V_out, su__prime_out, t_prime_u_out, t_u_out, tv__prime_out,
       \tØv_out , u_v__prime_out, uv__star_out, uv_prime_u_prime_v_out, \uØv_out ;

  not not_1 (not_1_out, T);
  not not_2 (not_2_out, S);
  not not_3 (not_3_out, U);
  not not_4 (not_4_out, V);
  nand tv__prime (tv__prime_out, V, T);
  nor s_u__prime (s_u__prime_out, U, S);
  xor uv_prime_u_prime_v (uv_prime_u_prime_v_out, V, U);
  nand uv__star (uv__star_out, U, V);
  or t_prime_u (t_prime_u_out, U, not_1_out);
  and and_1 (and_1_out, U, tv__prime_out);
  or t_u (t_u_out, T, U);
  and and_2 (and_2_out, T, uv_prime_u_prime_v_out);
  xor s_prime_t_st_prime (s_prime_t_st_prime_out, T, S);
  nand su__prime (su__prime_out, S, U);
  xnor \tØv  (\tØv_out , T, V);
  and and_3 (and_3_out, uv__star_out, T);
  nor u_v__prime (u_v__prime_out, V, U);
  and and_4 (and_4_out, T, s_u__prime_out);
  xnor s_v__prime (s_v__prime_out, S, V);
  and S_V (S_V_out, V, S, not_3_out);
  and and_5 (and_5_out, S, t_prime_u_out);
  and and_6 (and_6_out, not_1_out, s_v__prime_out);
  and and_7 (and_7_out, not_4_out, U);
  and and_8 (and_8_out, V, su__prime_out);
  xnor \uØv  (\uØv_out , U, V);
  or or_1 (or_1_out, \tØv_out , U, S);
  nor nor_1 (nor_1_out, V, T);
  and and_9 (and_9_out, S, t_u_out);
  and and_10 (and_10_out, S, not_3_out);
  and and_11 (and_11_out, \uØv_out , not_2_out);
  or or_2 (or_2_out, S_V_out, not_1_out, and_11_out);
  or or_3 (or_3_out, nor_1_out, and_7_out, and_9_out);
  nor nor_2 (nor_2_out, S, T);
  and and_12 (and_12_out, U, nor_2_out);
  _7_Segment_Display u_7_segment_display_1 (
    .g(or_4_out), .f(or_7_out), .a(or_1_out), .b(or_2_out), .e(or_3_out), .d(or_5_out), .c(or_6_out));  // open: dp
  or or_4 (or_4_out, and_5_out, and_1_out, and_4_out);
  or or_5 (or_5_out, and_12_out, and_10_out, and_6_out, and_2_out);
  or or_6 (or_6_out, s_u__prime_out, s_prime_t_st_prime_out, and_8_out);
  or or_7 (or_7_out, and_3_out, S, u_v__prime_out);

  // Notes on the sheet:
  //   e, d, c
  //   g, f, a, b
  //   38 gates
endmodule
