// Logisim project inf1400Oblig2,2-351.circ as structural Verilog: 2 circuits, main circuit main
module main (
  output out_1
);

  wire _1_out, _2_out, _3_out, _4_out, _5_out, _6_out, _7_out, Clk_out, clock_1_out, clock_2_out, d_ff_2_q,
       d_ff_3_q, kombinatorisk_logikk_1_da, kombinatorisk_logikk_1_db, kombinatorisk_logikk_1_y;
  wire [2:0] priority_encoder_1_out;

  Button _1 (.out(_1_out));
  Button _4 (.out(_4_out));
  Button _7 (.out(_7_out));
  Button button ();  // open: out
  Button _2 (.out(_2_out));
  Button _3 (.out(_3_out));
  Button _5 (.out(_5_out));
  Button _6 (.out(_6_out));
  Button _8 ();  // open: out
  Button _9 ();  // open: out
  Button _0 ();  // open: out
  Button button_2 ();  // open: out
  Clock clock_1 (.out(clock_1_out));
  Clock #(.highDuration(2), .lowDuration(2)) clock_2 (.out(clock_2_out));
  Priority_Encoder priority_encoder_1 (
    .in0(_1_out), .in1(_2_out), .in2(_3_out), .in3(_4_out), .in4(_5_out), .in5(_6_out), .in6(_7_out),
    .out(priority_encoder_1_out));  // open: in7, en_in, gs, en_out
  D_Flip_Flop d_ff_1 (.clk(clock_1_out), .D(clock_2_out), .Q(out_1));  // open: Qn, preset, en, reset
  Kombinatorisk_logikk kombinatorisk_logikk_1 (
    .Qa(d_ff_3_q), .Qb(d_ff_2_q), .X0(priority_encoder_1_out[0]), .X1(priority_encoder_1_out[1]),
    .X2(priority_encoder_1_out[2]), .Da(kombinatorisk_logikk_1_da), .Db(kombinatorisk_logikk_1_db),
    .y(kombinatorisk_logikk_1_y));
  Clock Clk (.out(Clk_out));
  D_Flip_Flop d_ff_2 (.clk(Clk_out), .D(kombinatorisk_logikk_1_da), .Q(d_ff_2_q));  // open: Qn, preset, en, reset
  D_Flip_Flop d_ff_3 (.clk(Clk_out), .D(kombinatorisk_logikk_1_db), .Q(d_ff_3_q));  // open: Qn, preset, en, reset
  LED led_1 (.in(kombinatorisk_logikk_1_y));

  // Notes on the sheet:
  //   Kode: 351
endmodule

module Kombinatorisk_logikk (
  input  Qa,
  input  Qb,
  input  X0,
  input  X1,
  input  X2,
  output Da,
  output Db,
  output y
);

  wire not_1_out, not_2_out, not_3_out, not_4_out, not_5_out;

  not not_1 (not_1_out, X0);
  not not_2 (not_2_out, X1);
  not not_3 (not_3_out, Qa);
  not not_4 (not_4_out, X1);
  not not_5 (not_5_out, Qb);
  and and_1 (Da, not_3_out, not_1_out, X2, X1, not_5_out);
  and and_2 (Db, Qb, X0, not_4_out, X2);
  and and_3 (y, Qa, not_1_out, not_2_out, X2);
endmodule
