// Logisim project inf1400Oblig2,2b-351.circ as structural Verilog: 3 circuits, main circuit main
module main (
);

  wire _1_out, _2_out, _3_out, _4_out, _5_out, _6_out, _7_out, and_1_out, and_2_out, Clk_out, j_k_ff_1_q,
       j_k_ff_2_q, kombinatorisk_logikk_1_da_riktig, kombinatorisk_logikk_1_db_feil,
       kombinatorisk_logikk_1_db_riktig, kombinatorisk_logikk_1_y_feil, kombinatorisk_logikk_1_y_riktig,
       or_1_out, priority_encoder_1_gs, venter_1_da_2, venter_1_db_2, venter_1_db_feil_2, venter_1_y_2,
       venter_1_y_feil_2;
  wire [2:0] priority_encoder_1_out;

  Button _1 (.out(_1_out));
  Button _4 (.out(_4_out));
  Button _7 (.out(_7_out));
  Button button ();  // open: out
  Button _3 (.out(_3_out));
  Button _2 (.out(_2_out));
  Button _5 (.out(_5_out));
  Button _6 (.out(_6_out));
  Button _8 ();  // open: out
  Button _9 ();  // open: out
  Button button_2 ();  // open: out
  Button _0 ();  // open: out
  Priority_Encoder priority_encoder_1 (
    .in1(_1_out), .in2(_2_out), .in3(_3_out), .in4(_4_out), .in5(_5_out), .in6(_6_out), .in7(_7_out),
    .out(priority_encoder_1_out), .gs(priority_encoder_1_gs));  // open: in0, en_in, en_out
  Kombinatorisk_logikk kombinatorisk_logikk_1 (
    .Qa(j_k_ff_2_q), .Qb(j_k_ff_1_q), .X2(priority_encoder_1_out[0]), .X1(priority_encoder_1_out[1]),
    .X0(priority_encoder_1_out[2]), .Trykket(priority_encoder_1_gs),
    .Db_FEIL(kombinatorisk_logikk_1_db_feil), .y_FEIL(kombinatorisk_logikk_1_y_feil),
    .Da_RIKTIG(kombinatorisk_logikk_1_da_riktig), .Db_RIKTIG(kombinatorisk_logikk_1_db_riktig),
    .y_RIKTIG(kombinatorisk_logikk_1_y_riktig));
  Clock Clk (.out(Clk_out));
  or or_1 (or_1_out, and_2_out, and_1_out);
  and and_1 (and_1_out, j_k_ff_1_q, venter_1_db_feil_2);
  Venter venter_1 (
    .Db_FEIL(kombinatorisk_logikk_1_db_feil), .Y_FEIL(kombinatorisk_logikk_1_y_feil),
    .Da(kombinatorisk_logikk_1_da_riktig), .Db(kombinatorisk_logikk_1_db_riktig),
    .y(kombinatorisk_logikk_1_y_riktig), .Clk(Clk_out), .Db_FEIL_2(venter_1_db_feil_2),
    .y_FEIL_2(venter_1_y_feil_2), .Da_2(venter_1_da_2), .Db_2(venter_1_db_2), .y_2(venter_1_y_2));
  J_K_Flip_Flop j_k_ff_1 (
    .J(venter_1_da_2), .clk(Clk_out), .K(or_1_out), .Q(j_k_ff_1_q));  // open: Qn, preset, en, reset
  J_K_Flip_Flop j_k_ff_2 (
    .J(venter_1_db_2), .clk(Clk_out), .K(or_1_out), .Q(j_k_ff_2_q));  // open: Qn, preset, en, reset
  and and_2 (and_2_out, j_k_ff_2_q, venter_1_y_feil_2);
  LED led_1 (.in(venter_1_y_2));

  // Notes on the sheet:
  //   Kode: 331
  //   K i JK-flippfloppen skal kun trykkes hvis IKKE riktig tall/knapp er trykket i riktig tilstand
endmodule

module Kombinatorisk_logikk (
  input  Qa,
  input  Qb,
  input  X2,
  input  X1,
  input  X0,
  input  Trykket,
  output Db_FEIL,
  output y_FEIL,
  output Da_RIKTIG,
  output Db_RIKTIG,
  output y_RIKTIG
);

  wire and_1_out, and_2_out, and_3_out, and_4_out, and_5_out, not_1_out, not_2_out, not_3_out, not_4_out,
       not_5_out;

  and and_1 (and_1_out, Trykket, Qa);
  and and_2 (and_2_out, Trykket, Qb);
  and and_3 (and_3_out, X2, Trykket);
  and and_4 (and_4_out, X1, Trykket);
  and and_5 (and_5_out, X0, Trykket);
  not not_1 (not_1_out, and_4_out);
  not not_2 (not_2_out, and_5_out);
  not not_3 (not_3_out, and_1_out);
  not not_4 (not_4_out, and_1_out);
  not not_5 (not_5_out, and_5_out);
  and and_6 (Da_RIKTIG, not_3_out, not_2_out, and_3_out, and_4_out);
  and and_7 (Db_RIKTIG, and_2_out, and_3_out, not_4_out, and_4_out, not_5_out);
  and and_8 (y_RIKTIG, and_1_out, and_3_out, and_2_out, not_1_out, not_2_out);
  xor xor_1 (Db_FEIL, Trykket, Db_RIKTIG);
  xor xor_2 (y_FEIL, Trykket, y_RIKTIG);
endmodule

module Venter (
  input  Db_FEIL,
  input  Y_FEIL,
  input  Da,
  input  Db,
  input  y,
  input  Clk,
  output Db_FEIL_2,
  output y_FEIL_2,
  output Da_2,
  output Db_2,
  output y_2
);

  wire d_ff_1_q, d_ff_2_q, d_ff_3_q, d_ff_4_q, d_ff_5_q, not_1_out, not_2_out, not_3_out, not_4_out,
       not_5_out;

  D_Flip_Flop d_ff_1 (.clk(Clk), .D(Db_FEIL), .Q(d_ff_1_q));  // open: Qn, preset, en, reset
  D_Flip_Flop d_ff_2 (.clk(Clk), .D(Y_FEIL), .Q(d_ff_2_q));  // open: Qn, preset, en, reset
  D_Flip_Flop d_ff_3 (.clk(Clk), .D(Da), .Q(d_ff_3_q));  // open: Qn, preset, en, reset
  D_Flip_Flop d_ff_4 (.clk(Clk), .D(Db), .Q(d_ff_4_q));  // open: Qn, preset, en, reset
  D_Flip_Flop d_ff_5 (.clk(Clk), .D(y), .Q(d_ff_5_q));  // open: Qn, preset, en, reset
  not not_1 (not_1_out, Db_FEIL);
  not not_2 (not_2_out, Y_FEIL);
  not not_3 (not_3_out, Da);
  not not_4 (not_4_out, Db);
  not not_5 (not_5_out, y);
  and and_1 (Db_FEIL_2, not_1_out, d_ff_1_q);
  and and_2 (y_FEIL_2, not_2_out, d_ff_2_q);
  and and_3 (Da_2, not_3_out, d_ff_3_q);
  and and_4 (Db_2, not_4_out, d_ff_4_q);
  and and_5 (y_2, not_5_out, d_ff_5_q);
endmodule
