// Logisim project inf1400Oblig2-351.circ as structural Verilog: 2 circuits, main circuit main
module main (
  output Out
);

  wire _1_2_out, _1_out, _2_out, _3_2_out, _3_out, _4_out, _5_2_out, _5_out, _6_out, _7_out, and_1_out,
       and_2_out, and_3_out, and_4_out, clock_1_out, enable_1_out_8, enable_1_out_9, enable_1_out_10,
       multiplexer_1_out, not_1_out, not_2_out, not_3_out, not_4_out, not_5_out, or_1_out, Trykket_out,
       xor_1_out;
  wire [1:0] s_r_ff_1_q;

  Button _1 (.out(_1_out));
  Button _4 (.out(_4_out));
  Button _7 (.out(_7_out));
  Button button ();  // open: out
  Button _2 (.out(_2_out));
  Button _3 (.out(_3_out));
  Button _6 (.out(_6_out));
  Button _5 (.out(_5_out));
  Button _9 ();  // open: out
  Button _8 ();  // open: out
  Button _0 ();  // open: out
  Button button_2 ();  // open: out
  Enable enable_1 (
    .in_1(_1_out), .in_2(_2_out), .in_3(_3_out), .in_4(_4_out), .in_5(_5_out), .in_6(_6_out), .in_7(_7_out),
    .out_8(enable_1_out_8), .out_9(enable_1_out_9), .out_10(enable_1_out_10));
  Clock clock_1 (.out(clock_1_out));
  or Trykket (Trykket_out, enable_1_out_8, enable_1_out_10, enable_1_out_9);
  not not_1 (not_1_out, enable_1_out_10);
  not not_2 (not_2_out, enable_1_out_9);
  not not_3 (not_3_out, enable_1_out_9);
  not not_4 (not_4_out, enable_1_out_10);
  and _3_2 (_3_2_out, enable_1_out_8, enable_1_out_9, not_1_out);
  and _5_2 (_5_2_out, enable_1_out_8, not_2_out, enable_1_out_10);
  and _1_2 (_1_2_out, enable_1_out_8, not_3_out, not_4_out);
  Multiplexer #(.select(2)) multiplexer_1 (
    .in0(_3_2_out), .in1(_5_2_out), .in3(_1_2_out), .out(multiplexer_1_out), .sel(s_r_ff_1_q));  // open: in2, en
  xor xor_1 (xor_1_out, Trykket_out, and_1_out);
  and and_1 (and_1_out, multiplexer_1_out, not_5_out);
  and and_2 (and_2_out, Trykket_out, Out);
  or or_1 (or_1_out, xor_1_out, and_2_out);
  S_R_Flip_Flop s_r_ff_1 (
    .S(and_1_out), .clk(clock_1_out), .R(or_1_out), .Q(s_r_ff_1_q[0]));  // open: Qn, preset, reset, en
  and and_3 (and_3_out, and_1_out, s_r_ff_1_q[0]);
  S_R_Flip_Flop s_r_ff_2 (
    .S(and_3_out), .clk(clock_1_out), .R(or_1_out), .Q(s_r_ff_1_q[1]));  // open: Qn, preset, reset, en
  and and_4 (and_4_out, and_1_out, s_r_ff_1_q[1]);
  S_R_Flip_Flop s_r_ff_3 (.S(and_4_out), .clk(clock_1_out), .R(or_1_out), .Q(Out));  // open: Qn, preset, reset, en
  not not_5 (not_5_out, Out);

  // Notes on the sheet:
  //   Kode: 351
  //   Denne lagde jeg før vi lærte om tillstandstabeller. Den funker fint men lyset skrur seg ikke av etter et kl signal og hvis du trykker 1 etter at utgangssignaley er av vil den ikke skru seg av.
  //   Tall 3
endmodule

module Enable (
  input  in_1,
  input  in_2,
  input  in_3,
  input  in_4,
  input  in_5,
  input  in_6,
  input  in_7,
  output out_8,
  output out_9,
  output out_10
);

  or or_1 (out_8, in_1, in_3, in_5, in_7);
  or or_2 (out_9, in_2, in_3, in_6, in_7);
  or or_3 (out_10, in_4, in_5, in_6, in_7);
endmodule
